# Fritzing sketch schema (saved by Fritzing 0.9.3b)
breadboards: 1

parts:
  Composant1 = Arduino Mega 2560 (Rev3)
  LED1 = LED - 5mm [color="Red (635nm)" package="5 mm [THT]"]
  LED2 = LED - 5mm [color="Green (555nm)" package="5 mm [THT]"]
  LED3 = LED - 5mm [color="Blue (430nm)" package="5 mm [THT]"]
  R3 = Resistor [tolerance=±5% resistance=220 package=THT]
  R4 = Resistor [tolerance=±5% resistance=220 package=THT]
  R5 = Resistor [tolerance=±5% resistance=220 package=THT]
  S1 = Pushbutton [package="[THT]"]
  R6 = Resistor [tolerance=±5% resistance=1k package=THT]
  R7 = Resistor [tolerance=±5% resistance=1k package=THT]  # not connected
  J1 = Piezo Speaker  # not connected

nets:
  N1: Composant1.5V, S1.Pin_3, S1.Pin_4
  N2: Composant1.GND, R3.Pin_1, R4.Pin_1, R5.Pin_1, R6.Pin_1
  N3: Composant1.D2_PWM, S1.Pin_1, S1.Pin_2, R6.Pin_0
  N4: Composant1.D5_PWM, LED1.cathode
  N5: Composant1.D6_PWM, LED2.cathode
  N6: Composant1.D7_PWM, LED3.cathode
  N7: LED1.anode, R5.Pin_0
  N8: LED2.anode, R4.Pin_0
  N9: LED3.anode, R3.Pin_0
